// Logisim project Meio Somador.circ as structural Verilog: 1 circuit, main circuit main
module main (
  input  A,
  input  B,
  output S,
  output Co
);

  xor xor_1 (S, A, B);
  and and_1 (Co, A, B);
endmodule
