// Logisim project Registrador 3 bits.circ as structural Verilog: 1 circuit, main circuit main
module main (
  input  S2,
  input  S1,
  input  S0,
  input  in_4,
  output S2_2,
  output S1_2,
  output S0_2
);

  FlipFlop_D_main Flip_Flop_2 (.D(S2), .CLK(in_4), .Q(S2_2));
  FlipFlop_D_main Flip_Flop_1 (.D(S1), .CLK(in_4), .Q(S1_2));
  FlipFlop_D_main Flip_Flop_0 (.D(S0), .CLK(in_4), .Q(S0_2));
endmodule
