// Logisim project Somador 3 bits.circ as structural Verilog: 1 circuit, main circuit main
module main (
  input  A2,
  input  B2,
  input  A1,
  input  B1,
  input  A0,
  input  B0,
  output Carry,
  output S2,
  output S1,
  output S0
);

  wire main_2_co, main_3_co;

  Somador_Completo_main main_1 (.A(A2), .B(B2), .Ci(main_2_co), .Co(Carry), .S(S2));
  Somador_Completo_main main_2 (.A(A1), .B(B1), .Ci(main_3_co), .Co(main_2_co), .S(S1));
  Meio_Somador_main main_3 (.A(A0), .B(B0), .S(S0), .Co(main_3_co));
endmodule
