// Logisim project ckt d.circ as structural Verilog: 1 circuit, main circuit main
module main (
  input  C,
  input  B,
  input  A,
  output out_4
);

  wire and_1_out, and_2_out;

  and and_1 (and_1_out, ~B, ~A);  // AND_Gate
  and and_2 (and_2_out, B, A);
  or or_1 (out_4, ~C, and_1_out, and_2_out);  // OR_Gate
endmodule
