// Logisim project ckt g.circ as structural Verilog: 1 circuit, main circuit main
module main (
  input  C,
  input  B,
  input  A,
  output out_4
);

  wire and_1_out;

  and and_1 (and_1_out, ~C, A);  // AND_Gate
  or or_1 (out_4, C, ~B, and_1_out);  // OR_Gate
endmodule
