// Logisim project main.circ as structural Verilog: 1 circuit, main circuit main
module main (
  input  in_1,
  input  in_2,
  input  in_3,
  input  in_4,
  input  in_5,
  input  in_6
);

  wire clock_1_out, main_1_s0, main_1_s1, main_1_s2, main_2_s0_2, main_2_s1_2, main_2_s2_2, main_3_out_4,
       main_3_out_5, main_3_out_6, main_3_out_7, main_3_out_8, main_3_out_9, main_3_out_10;

  Somador_3_bits_main main_1 (
    .A2(in_1), .B2(in_4), .A1(in_2), .B1(in_5), .A0(in_3), .B0(in_6), .S2(main_1_s2), .S1(main_1_s1),
    .S0(main_1_s0));  // open: Carry
  Clock clock_1 (.out(clock_1_out));
  Registrador_3_bits_main main_2 (
    .in_4(clock_1_out), .S2_2(main_2_s2_2), .S2(main_1_s2), .S1(main_1_s1), .S1_2(main_2_s1_2),
    .S0_2(main_2_s0_2), .S0(main_1_s0));
  Conversor_7_segmentos_main main_3 (
    .C(main_2_s2_2), .B(main_2_s1_2), .A(main_2_s0_2), .out_4(main_3_out_4), .out_5(main_3_out_5),
    .out_6(main_3_out_6), .out_7(main_3_out_7), .out_8(main_3_out_8), .out_9(main_3_out_9),
    .out_10(main_3_out_10));
  _7_Segment_Display u_7_segment_display_1 (
    .g(main_3_out_5), .f(main_3_out_7), .a(main_3_out_9), .b(main_3_out_4), .e(main_3_out_6),
    .d(main_3_out_8), .c(main_3_out_10));  // open: dp

  // Notes on the sheet:
  //   B1
  //   B2
  //   B0
  //   S1
  //   S2
  //   S0
  //   A2
  //   A0
  //   A1
  //   Carry
  //   CLK
  //   S2
  //   S1
  //   S0
  //   S2
  //   S1
  //   S0
endmodule
