// Logisim project Conversor 7 segmentos.circ as structural Verilog: 1 circuit, main circuit main
module main (
  input  C,
  input  B,
  input  A,
  output out_4,
  output out_5,
  output out_6,
  output out_7,
  output out_8,
  output out_9,
  output out_10
);

  ckt_a_main main_1 (.C(C), .B(B), .A(A), .out_4(out_5));
  ckt_b_main main_2 (.C(C), .B(B), .A(A), .out_4(out_7));
  ckt_c_main main_3 (.C(C), .B(B), .A(A), .out_4(out_9));
  ckt_d_main main_4 (.C(C), .B(B), .A(A), .out_4(out_4));
  ckt_e_main main_5 (.C(C), .B(B), .A(A), .out_4(out_6));
  ckt_f_main main_6 (.C(C), .B(B), .A(A), .out_4(out_8));
  ckt_g_main main_7 (.C(C), .B(B), .A(A), .out_4(out_10));
endmodule
