// Logisim project FlipFlop D.circ as structural Verilog: 1 circuit, main circuit main
module main (
  input  D,
  input  CLK,
  output Q
);

  wire Mestre_q, not_1_out;

  not not_1 (not_1_out, CLK);
  Latch_D_main Mestre (.D(D), .C(not_1_out), .Q(Mestre_q));
  Latch_D_main Escravo (.D(Mestre_q), .C(CLK), .Q(Q));

  // Notes on the sheet:
  //   Qm
  //   Dm
  //   Cm
  //   Ds
  //   Cs
  //   Qs
endmodule
