// Logisim project ckt c.circ as structural Verilog: 1 circuit, main circuit main
module main (
  input  C,
  input  B,
  input  A,
  output out_4
);

  wire and_1_out, and_2_out;

  and and_1 (and_1_out, C, A);
  and and_2 (and_2_out, ~C, ~A);  // AND_Gate
  or or_1 (out_4, and_1_out, B, and_2_out);
endmodule
