// Logisim project ckt f.circ as structural Verilog: 1 circuit, main circuit main
module main (
  input  C,
  input  B,
  input  A,
  output out_4
);

  wire and_1_out, and_2_out, and_3_out, and_4_out;

  and and_1 (and_1_out, ~C, ~A);  // AND_Gate
  and and_2 (and_2_out, ~C, B);  // AND_Gate
  and and_3 (and_3_out, B, ~A);  // AND_Gate
  and and_4 (and_4_out, C, ~B, A);  // AND_Gate
  or or_1 (out_4, and_1_out, and_2_out, and_3_out, and_4_out);
endmodule
